// Digital circuit 1)_Mux_8_Inputs.dig as structural Verilog
module _1__Mux_8_Inputs (
  input  D0,
  input  D1,
  input  D2,
  input  D3,
  input  D4,
  input  D5,
  input  D6,
  input  D7,
  input  Sel0,
  input  Sel1,
  input  Sel2,
  output Out
);

  wire and_1_out, and_2_out, and_3_out, and_4_out, and_5_out, and_6_out, and_7_out, and_8_out, not_1_out,
       not_2_out, not_3_out, or_1_out, or_2_out;

  not not_1 (not_1_out, Sel2);
  not not_2 (not_2_out, Sel1);
  not not_3 (not_3_out, Sel0);
  and and_1 (and_1_out, D7, Sel2, Sel1, Sel0);
  and and_2 (and_2_out, D6, Sel2, Sel1, not_3_out);
  and and_3 (and_3_out, D5, Sel2, not_2_out, Sel0);
  and and_4 (and_4_out, D4, Sel2, not_2_out, not_3_out);
  and and_5 (and_5_out, D3, not_1_out, Sel1, Sel0);
  and and_6 (and_6_out, D2, not_1_out, Sel1, not_3_out);
  and and_7 (and_7_out, D1, not_1_out, not_2_out, Sel0);
  and and_8 (and_8_out, D0, not_1_out, not_2_out, not_3_out);
  or or_1 (or_1_out, and_1_out, and_2_out, and_3_out, and_4_out);
  or or_2 (or_2_out, and_5_out, and_6_out, and_7_out, and_8_out);
  xor xor_1 (Out, or_1_out, or_2_out);

  // Notes on the sheet:
  //   Se toma la idea base del Multiplexor de 4 entradas, y
  //   es extrapolada. Se hacen las conexiones de forma 
  //   que cada una de las entradas de la 0 a la 7, tenga su 
  //   representación en un número binario dado por los
  //   selectores.
  //   Finalmente, como el ejercicio condiciona usar 
  //   compuertas de máximo 4 entradas, se recogen 4 con
  //   un OR (4 In) y las otras 4 con otro OR (4 In);  estas se 
  //   hacen converger en un XOR final de 2 entradas.
  //   Si al final se hubiera escogido un OR en lugar del XOR,
  //   funcionaría igual dado que cada entrada es controlada
  //   por una combinación única que llega a su AND.
endmodule
