// Digital circuit 2)_Demux_4_Outputs.dig as structural Verilog
module _2__Demux_4_Outputs (
  input  D,
  input  Sel1,
  input  Sel0,
  output Out3,
  output Out2,
  output Out1,
  output Out0
);

  wire not_1_out, not_2_out;

  not not_1 (not_1_out, Sel1);
  not not_2 (not_2_out, Sel0);
  and and_1 (Out3, D, Sel1, Sel0);
  and and_2 (Out2, D, Sel1, not_2_out);
  and and_3 (Out1, D, not_1_out, Sel0);
  and and_4 (Out0, D, not_1_out, not_2_out);

  // Notes on the sheet:
  //   El Demultiplexor tiene como idea esencial una 
  //   igual a la del Multiplexor, que es controlar la 
  //   comunicación de una entrada por medio de
  //   selectores. Pero en este caso es una única
  //   entrada y hay varias salidas, del 0 a la 3 
  //   controladas por una combinación de selectores
  //   que representa a su número binario.
  //   Por ejemplo, teniendo "Sel1" y "Sel0" en 1 y 0
  //   respectivamente, tenemos el 10 que representa
  //   al 2 en binario, teniendo así activa la salida Out2.
endmodule
