// Digital circuit 3)_Flip_Flop_JK.dig as structural Verilog
module _3__Flip_Flop_JK (
  input  K,
  input  J,
  input  Clock,
  output Q,
  output Q_2
);

  wire nand_1_out, nand_2_out, nand_3_out, nand_4_out, nand_5_out, nand_6_out, nand_7_out, nand_8_out,
       not_1_out, not_2_out, not_3_out;

  nand nand_1 (nand_1_out, Q, J);
  nand nand_2 (nand_2_out, K, Q_2);
  not not_1 (not_1_out, nand_1_out);
  not not_2 (not_2_out, nand_2_out);
  nand nand_3 (nand_3_out, not_1_out, Clock);
  nand nand_4 (nand_4_out, Clock, not_2_out);
  not not_3 (not_3_out, Clock);
  nand nand_5 (nand_5_out, nand_3_out, nand_6_out);
  nand nand_6 (nand_6_out, nand_5_out, nand_4_out);
  nand nand_7 (nand_7_out, nand_5_out, not_3_out);
  nand nand_8 (nand_8_out, not_3_out, nand_6_out);
  nand nand_9 (Q_2, nand_7_out, Q);
  nand nand_10 (Q, Q_2, nand_8_out);

  // Notes on the sheet:
  //   El Flip Flop JK tiene las mismas capacidades del RS, pero
  //   soluciona el problema de estado indeterminado.
  //   + J=0 y K=0, se mantiene el estado de Q. 
  //   + J=1 y K=0, se establece Q=1. 
  //   + J=0 y K=1, se resetea, quedando Q=0.
  //   + J=1 y K=1, responde complementando Q, es decir si Q=0, 
  //       tras el ciclo de reloj Q=1, y cuando Q=1 tras el ciclo Q=0.
endmodule
