// Digital circuit 3)_Flip_Flop_RS.dig as structural Verilog
module _3__Flip_Flop_RS (
  input  R,
  input  S,
  input  Clock,
  output Q,
  output Q_2
);

  wire nand_1_out, nand_2_out, nand_3_out, nand_4_out, nand_5_out, nand_6_out, not_1_out;

  nand nand_1 (nand_1_out, S, Clock);
  nand nand_2 (nand_2_out, Clock, R);
  not not_1 (not_1_out, Clock);
  nand nand_3 (nand_3_out, nand_1_out, nand_4_out);
  nand nand_4 (nand_4_out, nand_3_out, nand_2_out);
  nand nand_5 (nand_5_out, nand_3_out, not_1_out);
  nand nand_6 (nand_6_out, not_1_out, nand_4_out);
  nand nand_7 (Q_2, nand_5_out, Q);
  nand nand_8 (Q, Q_2, nand_6_out);

  // Notes on the sheet:
  //   El Flip Flop RS (Reset-Set) permite almacenar estados, 
  //   establacerlos o resetearlos cada ciclo de reloj:
  //   + R=0 y S=0, se mantiene el estado de Q. 
  //   + R=1 y S=0, se resetea, quedando Q=0. 
  //   + R=0 y S=1, se establece Q=1.
  //   + R=1 y S=1, entra en estado indeterminado.
endmodule
