// Digital circuit 4)_Pin_IO_System.dig as structural Verilog
module _4__Pin_IO_System (
  input  Set,
  input  D0,
  input  Enable,
  input  Clear,
  input  D2,
  input  D3,
  input  D1,
  input  Clock,
  input  Clock_Inputs,
  input  Clock_Outputs,
  input  In_0,
  input  Out_0,
  input  In_1,
  input  Out_1,
  input  In_2,
  input  Out_2,
  input  In_3,
  input  Out_3,
  input  Enable_Inputs,
  input  Clear_Inputs,
  input  Enable_Outputs,
  input  Clear_Outputs,
  input  Set_Inputs,
  input  Set_Outputs,
  output In,
  output In_4,
  output In_5,
  output In_6,
  output Out,
  output Out_4,
  output Out_5,
  output Out_6
);

  wire Input_0, Input_1, Input_2, Input_3, multiplexer_1_out, multiplexer_2_out, multiplexer_3_out,
       multiplexer_4_out, multiplexer_5_out, multiplexer_6_out, multiplexer_7_out, multiplexer_8_out,
       multiplexer_9_out, multiplexer_10_out, multiplexer_11_out, multiplexer_12_out, Output_0, Output_1,
       Output_2, Output_3, Pin_0, Pin_1, Pin_2, Pin_3;

  PullDown pulldown_1 (.out(Input_3));
  Multiplexer multiplexer_1 (.sel(Enable_Inputs), .in_0(In), .in_1(Input_3), .out(multiplexer_1_out));
  D_FF_AS d_ff_as_1 (
    .Set(Set_Inputs), .D(multiplexer_1_out), .C(Clock_Inputs), .Clr(Clear_Inputs), .Q(In));  // open: nQ
  PullDown pulldown_2 (.out(Input_2));
  Multiplexer multiplexer_2 (.sel(Enable_Inputs), .in_0(In_4), .in_1(Input_2), .out(multiplexer_2_out));
  D_FF_AS d_ff_as_2 (
    .Set(Set_Inputs), .D(multiplexer_2_out), .C(Clock_Inputs), .Clr(Clear_Inputs), .Q(In_4));  // open: nQ
  PullDown pulldown_3 (.out(Input_1));
  Multiplexer multiplexer_3 (.sel(Enable), .in_0(Pin_3), .in_1(D3), .out(multiplexer_3_out));
  Multiplexer multiplexer_4 (.sel(Enable_Inputs), .in_0(In_5), .in_1(Input_1), .out(multiplexer_4_out));
  D_FF_AS d_ff_as_3 (.Set(Set), .D(multiplexer_3_out), .C(Clock), .Clr(Clear), .Q(Pin_3));  // open: nQ
  D_FF_AS d_ff_as_4 (
    .Set(Set_Inputs), .D(multiplexer_4_out), .C(Clock_Inputs), .Clr(Clear_Inputs), .Q(In_5));  // open: nQ
  PullDown pulldown_4 (.out(Input_0));
  Multiplexer multiplexer_5 (.sel(Enable), .in_0(Pin_2), .in_1(D2), .out(multiplexer_5_out));
  Multiplexer multiplexer_6 (.sel(Enable_Inputs), .in_0(In_6), .in_1(Input_0), .out(multiplexer_6_out));
  D_FF_AS d_ff_as_5 (.Set(Set), .D(multiplexer_5_out), .C(Clock), .Clr(Clear), .Q(Pin_2));  // open: nQ
  D_FF_AS d_ff_as_6 (
    .Set(Set_Inputs), .D(multiplexer_6_out), .C(Clock_Inputs), .Clr(Clear_Inputs), .Q(In_6));  // open: nQ
  Multiplexer multiplexer_7 (.sel(Enable), .in_0(Pin_1), .in_1(D1), .out(multiplexer_7_out));
  D_FF_AS d_ff_as_7 (.Set(Set), .D(multiplexer_7_out), .C(Clock), .Clr(Clear), .Q(Pin_1));  // open: nQ
  Multiplexer multiplexer_8 (.sel(Enable), .in_0(Pin_0), .in_1(D0), .out(multiplexer_8_out));
  PullDown pulldown_5 (.out(Output_3));
  D_FF_AS d_ff_as_8 (.Set(Set), .D(multiplexer_8_out), .C(Clock), .Clr(Clear), .Q(Pin_0));  // open: nQ
  Multiplexer multiplexer_9 (.sel(Enable_Outputs), .in_0(Out), .in_1(Output_3), .out(multiplexer_9_out));
  D_FF_AS d_ff_as_9 (
    .Set(Set_Outputs), .D(multiplexer_9_out), .C(Clock_Outputs), .Clr(Clear_Outputs), .Q(Out));  // open: nQ
  PullDown pulldown_6 (.out(Output_2));
  Multiplexer multiplexer_10 (.sel(Enable_Outputs), .in_0(Out_4), .in_1(Output_2), .out(multiplexer_10_out));
  assign Output_0 = Pin_0 ? Out_0 : 1'bz;  // Driver driver_1
  assign Input_0 = ~Pin_0 ? In_0 : 1'bz;  // DriverInvSel driverinvsel_1
  assign Output_2 = Pin_2 ? Out_2 : 1'bz;  // Driver driver_2
  assign Input_2 = ~Pin_2 ? In_2 : 1'bz;  // DriverInvSel driverinvsel_2
  D_FF_AS d_ff_as_10 (
    .Set(Set_Outputs), .D(multiplexer_10_out), .C(Clock_Outputs), .Clr(Clear_Outputs), .Q(Out_4));  // open: nQ
  PullDown pulldown_7 (.out(Output_1));
  Multiplexer multiplexer_11 (.sel(Enable_Outputs), .in_0(Out_5), .in_1(Output_1), .out(multiplexer_11_out));
  D_FF_AS d_ff_as_11 (
    .Set(Set_Outputs), .D(multiplexer_11_out), .C(Clock_Outputs), .Clr(Clear_Outputs), .Q(Out_5));  // open: nQ
  PullDown pulldown_8 (.out(Output_0));
  assign Output_1 = Pin_1 ? Out_1 : 1'bz;  // Driver driver_3
  assign Input_1 = ~Pin_1 ? In_1 : 1'bz;  // DriverInvSel driverinvsel_3
  assign Output_3 = Pin_3 ? Out_3 : 1'bz;  // Driver driver_4
  assign Input_3 = ~Pin_3 ? In_3 : 1'bz;  // DriverInvSel driverinvsel_4
  Multiplexer multiplexer_12 (.sel(Enable_Outputs), .in_0(Out_6), .in_1(Output_0), .out(multiplexer_12_out));
  D_FF_AS d_ff_as_12 (
    .Set(Set_Outputs), .D(multiplexer_12_out), .C(Clock_Outputs), .Clr(Clear_Outputs), .Q(Out_6));  // open: nQ

  // Notes on the sheet:
  //   In: pin 3
  //   In_4: pin 2
  //   In_5: pin 1
  //   Out: pin 3
  //   Out_4: pin 2
  //   Out_5: pin 1
  //   NOTA
  //   1) La resistencias de pull-down se implementaron
  //   para evitar que algunos registros se pusieran en 
  //   alto de la nada, al parecer, en ciertas  condiciones
  //   el estado de alta impedancia generaba esto.
  //   2) Inicialmente planeaba que hubiera un solo
  //   boton de Enable y de Clear para los 3 registros, 
  //   para así habilitar o limpiar todo a la vez, pero tras 
  //   hacer pruebas esto presentaba bugs y aparecian 
  //   estados en alto para pines que ni habilitados estaban.
  //   Registro Almacen Entrada
  //   Registro de Configuración
  //   0 == Entrada
  //   1 == Salida
  //   Estados para 
  //   Entradas o Salidas
  //   Registro Control Salida
endmodule
